# Fritzing sketch Schematic_1 (saved by Fritzing 0.8.7b)
breadboards: 1

parts:
  Part1 = Arduino Uno (Rev3)
  U1 = LCD-16X2 [package=lcd-16x2]
  LCM1602_IIC1 = LCM1602 IIC [part_number="LCM1602 IIC" chip_label="LCM1602 IIC" package="DIP (Dual Inline) [THT]"]

nets:
  N1: Part1.A4/SDA, LCM1602_IIC1.SDA, LCM1602_IIC1.LED_B
  N2: Part1.A5/SCL, LCM1602_IIC1.SCL
  GND: Part1.GND, LCM1602_IIC1.GND
  5V: Part1.5V, LCM1602_IIC1.VCC, LCM1602_IIC1.LED_A
  VSS: U1.VSS, LCM1602_IIC1.VSS
  VDD: U1.VDD, LCM1602_IIC1.VDD
  N3: U1.VO, LCM1602_IIC1.V0
  N4: U1.RS, LCM1602_IIC1.RS
  N5: U1.R_W, LCM1602_IIC1.RW
  N6: U1.E, LCM1602_IIC1.E
  N7: U1.DB0, LCM1602_IIC1.D0
  N8: U1.DB1, LCM1602_IIC1.D1
  N9: U1.DB2, LCM1602_IIC1.D2
  N10: U1.DB3, LCM1602_IIC1.D3
  N11: U1.DB4, LCM1602_IIC1.D4
  N12: U1.DB5, LCM1602_IIC1.D5
  N13: U1.DB6, LCM1602_IIC1.D6
  N14: U1.DB7, LCM1602_IIC1.D7
  N15: U1.A, LCM1602_IIC1.A
  N16: U1.K, LCM1602_IIC1.K

custom parts:
  LCM1602 IIC: I2C-Module to use a 1602 or 2004 LCD on with the wire.h libory Serial LCD Modul
